# Fritzing sketch Jalousie_control (saved by Fritzing 0.9.3b)

parts:
  Часть1 = BluePill
  BT2 = Bluetooth HC-06u [package=THT]
  Часть2 = BH1750
  SERVO1 = Tower Pro SG90 servo [part_number=101246]

nets:
  N1: Часть1.B10, Часть2.SCL
  N2: Часть1.B11, Часть2.SDA
  3V3: Часть1.3V3, Часть2.VCC
  GND: Часть1.GND, Часть2.GND
  GND2: Часть1.GND2, SERVO1.GND
  N3: Часть1.3V31, BT2.VCC
  GND3: Часть1.GND3, BT2.GND
  5V: Часть1.5V, SERVO1.+5V
  N4: Часть1.B6, SERVO1.Signal
  N5: Часть1.A10, BT2.TXD
  N6: Часть1.A9, BT2.RXD

custom parts:
  Bluetooth HC-06u: Bluetooth HC-06 - face up, pins down 16.5mm x 37.5mm PCB
  BH1750: Light Sensor
  Tower Pro SG90 servo: Original file by John De Cristofaro http://www.adafruit.com/products/1449 Adafruit Feedback Servo (Small) Edited by: e-radionica.com 28/9/2015
